# Fritzing sketch Expérience 1 FRITZ - Copie (saved by Fritzing 0.9.3b)
breadboards: 1

parts:
  Composant1 = Arduino Uno (Rev3)
  R2 = Resistor [tolerance=±5% resistance=220 package=THT]
  L1 = Inductor [package="400 mil [THT]"]
  R1 = Resistor [tolerance=±5% resistance=220 package=THT]

nets:
  N1: Composant1.A0, Composant1.D9_PWM, R2.Pin_1, L1.pin_0, L1.pin_1, R1.Pin_0, R1.Pin_1
  N2: Composant1.GND, R2.Pin_0
