# Fritzing sketch Expérience 2 FRITZ - Copie (saved by Fritzing 0.9.3b)
breadboards: 1

parts:
  Composant1 = Arduino Uno (Rev3)
  R1 = Resistor [tolerance=±5% resistance=1k package=THT]
  R2 = Resistor [tolerance=±5% resistance=3.3k package=THT]
  L1 = Inductor [package="400 mil [THT]"]
  D1 = Rectifier Diode [part_number=1N4001 package="300 mil [THT]"]
  R3 = Resistor [tolerance=±5% resistance=1M package=THT]
  C1 = Ceramic Capacitor [capacitance=100nF package="100 mil [THT, multilayer]"]
  C2 = Ceramic Capacitor [capacitance=100nF package="100 mil [THT, multilayer]"]

nets (from the schematic view):
  N1: Composant1.A0, D1.cathode, R3.Pin_1, C2.1
  N2: Composant1.D9_PWM, R1.Pin_1
  N3: Composant1.GND, R2.Pin_0, R3.Pin_0, C2.0
  N4: R1.Pin_0, R2.Pin_1, L1.pin_1
  N5: L1.pin_0, D1.anode, C1.0
