# Fritzing sketch Expérience finale FRITZ (saved by Fritzing 0.9.3b)
breadboards: 1

parts:
  Composant1 = Arduino Uno (Rev3)
  R1 = Resistor [tolerance=±5% resistance=1k package=THT]
  R2 = Resistor [tolerance=±5% resistance=3.3k package=THT]
  L1 = Inductor [package="400 mil [THT]"]
  D1 = Rectifier Diode [part_number=1N4001 package="300 mil [THT]"]
  R3 = Resistor [tolerance=±5% resistance=1M package=THT]
  C1 = Ceramic Capacitor [capacitance=100nF package="100 mil [THT, multilayer]"]
  C2 = Ceramic Capacitor [capacitance=100nF package="100 mil [THT, multilayer]"]
  LED1 = LED - 5mm [color="Red (633nm)" package="5 mm [THT]"]
  LED2 = LED - 5mm [color="Red (633nm)" package="5 mm [THT]"]
  LED3 = LED - 5mm [color="Red (633nm)" package="5 mm [THT]"]

nets (from the breadboard view):
  N1: Composant1.A0, D1.cathode, R3.Pin_1, C2.0
  N2: Composant1.D9_PWM, R1.Pin_1
  N3: Composant1.D10_PWM/SS, LED1.cathode
  N4: Composant1.D11_PWM/MOSI, LED3.cathode
  N5: Composant1.D12/MISO, LED2.cathode
  N6: Composant1.GND, R2.Pin_0, R3.Pin_0, C2.1, LED1.anode, LED2.anode, LED3.anode
  N7: R2.Pin_1, L1.pin_0
  N8: L1.pin_1, D1.anode, C1.1
